// Digital circuit PRAKTIKUM-5,1.dig as structural Verilog
module PRAKTIKUM_5_1 (
  input  A,
  input  B
);

  wire and_1_out, or_1_out, or_2_out, or_3_out;

  or or_1 (or_1_out, A, B);
  or or_2 (or_2_out, A, ~B);  // Or
  or or_3 (or_3_out, ~A, B);  // Or
  and and_1 (and_1_out, or_1_out, or_2_out, or_3_out);
  LED X (.in(and_1_out));
endmodule
