// Digital circuit PRAKTIKUM-5.dig as structural Verilog
module PRAKTIKUM_5 (
  input  A,
  input  B,
  input  C
);

  wire and_1_out, and_2_out, or_1_out, or_2_out;

  and and_1 (and_1_out, ~B, C);  // And
  or or_1 (or_1_out, A, ~C);  // Or
  and and_2 (and_2_out, and_1_out, or_1_out);
  or or_2 (or_2_out, A, and_2_out, B);
  LED led (.in(or_2_out));
endmodule
